// Digital circuit EX_MEM Reg.dig as structural Verilog
module EX_MEM_Reg (
  input  CLK,
  input  Jump,
  input  Branch,
  input  MemRead,
  input  MemToReg,
  input  MemWrite,
  input  RegWrite,
  input  [31:0] BranchAmt,
  input  Zero,
  input  [31:0] ALUResult,
  input  [31:0] RD2,
  input  [4:0] RegDst,
  input  [31:0] JmpAddr,
  output JumpOut,
  output BranchOut,
  output MemReadOut,
  output MemToRegOut,
  output MemWriteOut,
  output RegWriteOut,
  output [31:0] BranchAmtOut,
  output ZeroOut,
  output [31:0] ALUResultOut,
  output [31:0] RD2Out,
  output [4:0] RegDstOut,
  output [31:0] JmpAddrOut
);

  wire Branch_nq, Jump_nq, MemRead_nq, MemToReg_nq, MemWrite_nq, RegWrite_nq, Zero_nq;
  wire [4:0] RegDst_nq;
  wire [31:0] ALUResult_nq, BranchAmt_nq, Jump_Address_nq, RD2_nq;

  D_FF u_Jump (.D(Jump), .C(CLK), .Q(JumpOut), .nQ(Jump_nq));
  D_FF u_Branch (.D(Branch), .C(CLK), .Q(BranchOut), .nQ(Branch_nq));
  D_FF u_MemRead (.D(MemRead), .C(CLK), .Q(MemReadOut), .nQ(MemRead_nq));
  D_FF u_MemToReg (.D(MemToReg), .C(CLK), .Q(MemToRegOut), .nQ(MemToReg_nq));
  D_FF u_MemWrite (.D(MemWrite), .C(CLK), .Q(MemWriteOut), .nQ(MemWrite_nq));
  D_FF u_RegWrite (.D(RegWrite), .C(CLK), .Q(RegWriteOut), .nQ(RegWrite_nq));
  D_FF #(.Bits(32)) u_BranchAmt (.D(BranchAmt), .C(CLK), .Q(BranchAmtOut), .nQ(BranchAmt_nq));
  D_FF u_Zero (.D(Zero), .C(CLK), .Q(ZeroOut), .nQ(Zero_nq));
  D_FF #(.Bits(32)) u_ALUResult (.D(ALUResult), .C(CLK), .Q(ALUResultOut), .nQ(ALUResult_nq));
  D_FF #(.Bits(32)) u_RD2 (.D(RD2), .C(CLK), .Q(RD2Out), .nQ(RD2_nq));
  D_FF #(.Bits(5)) u_RegDst (.D(RegDst), .C(CLK), .Q(RegDstOut), .nQ(RegDst_nq));
  D_FF #(.Bits(32)) Jump_Address (.D(JmpAddr), .C(CLK), .Q(JmpAddrOut), .nQ(Jump_Address_nq));
  // Pins of 1 and 32 bits meet at BranchAmt_nq
  // Pins of 1 and 32 bits meet at ALUResult_nq
  // Pins of 1 and 32 bits meet at RD2_nq
  // Pins of 1 and 5 bits meet at RegDst_nq
  // Pins of 1 and 32 bits meet at Jump_Address_nq
  // also tied to GND on the sheet: {RegWrite_nq, BranchAmt_nq[0], Zero_nq, ALUResult_nq[0], RD2_nq[0], RegDst_nq[0], Jump_Address_nq[0], MemWrite_nq, MemToReg_nq, MemRead_nq, Branch_nq, Jump_nq}
endmodule
