// Digital circuit ID_EX Reg.dig as structural Verilog
module ID_EX_Reg (
  input  Jump,
  input  RegDst,
  input  Branch,
  input  MemRead,
  input  MemToReg,
  input  [3:0] ALUOp,
  input  MemWrite,
  input  ALUSrc,
  input  RegWrite,
  input  [31:0] PC,
  input  [31:0] RD1,
  input  [31:0] RD2,
  input  [31:0] Imm,
  input  [4:0] Rt,
  input  [4:0] Rd,
  input  [31:0] JmpAddr,
  input  CLK,
  output JumpOut,
  output RegDstOut,
  output BranchOut,
  output MemReadOut,
  output MemToRegOut,
  output [3:0] ALUOpOut,
  output MemWriteOut,
  output ALUSrcOut,
  output RegWriteOut,
  output [31:0] PCOut,
  output [31:0] RD1Out,
  output [31:0] RD2Out,
  output [31:0] ImmOut,
  output [4:0] RtOut,
  output [4:0] RdOut,
  output [31:0] JmpAddrOut
);

  wire ALUSrc_nq, Branch_nq, Jump_nq, MemRead_nq, MemToReg_nq, MemWrite_nq, RegDst_nq, RegWrite_nq;
  wire [3:0] ALUOp_nq;
  wire [4:0] Rd_nq, Rt_nq;
  wire [31:0] Imm_nq, Jump_Address_nq, PC_plus_4_nq, ReadData1_nq, ReadData2_nq;

  D_FF u_Jump (.D(Jump), .C(CLK), .Q(JumpOut), .nQ(Jump_nq));
  D_FF u_RegDst (.D(RegDst), .C(CLK), .Q(RegDstOut), .nQ(RegDst_nq));
  D_FF u_Branch (.D(Branch), .C(CLK), .Q(BranchOut), .nQ(Branch_nq));
  D_FF u_MemRead (.D(MemRead), .C(CLK), .Q(MemReadOut), .nQ(MemRead_nq));
  D_FF u_MemToReg (.D(MemToReg), .C(CLK), .Q(MemToRegOut), .nQ(MemToReg_nq));
  D_FF #(.Bits(4)) u_ALUOp (.D(ALUOp), .C(CLK), .Q(ALUOpOut), .nQ(ALUOp_nq));
  D_FF u_MemWrite (.D(MemWrite), .C(CLK), .Q(MemWriteOut), .nQ(MemWrite_nq));
  D_FF u_ALUSrc (.D(ALUSrc), .C(CLK), .Q(ALUSrcOut), .nQ(ALUSrc_nq));
  D_FF u_RegWrite (.D(RegWrite), .C(CLK), .Q(RegWriteOut), .nQ(RegWrite_nq));
  D_FF #(.Bits(32)) PC_plus_4 (.D(PC), .C(CLK), .Q(PCOut), .nQ(PC_plus_4_nq));
  D_FF #(.Bits(32)) ReadData1 (.D(RD1), .C(CLK), .Q(RD1Out), .nQ(ReadData1_nq));
  D_FF #(.Bits(32)) ReadData2 (.D(RD2), .C(CLK), .Q(RD2Out), .nQ(ReadData2_nq));
  D_FF #(.Bits(32)) u_Imm (.D(Imm), .C(CLK), .Q(ImmOut), .nQ(Imm_nq));
  D_FF #(.Bits(5)) u_Rt (.D(Rt), .C(CLK), .Q(RtOut), .nQ(Rt_nq));
  D_FF #(.Bits(5)) u_Rd (.D(Rd), .C(CLK), .Q(RdOut), .nQ(Rd_nq));
  D_FF #(.Bits(32)) Jump_Address (.D(JmpAddr), .C(CLK), .Q(JmpAddrOut), .nQ(Jump_Address_nq));
  // Pins of 1 and 32 bits meet at ReadData1_nq
  // Pins of 1 and 32 bits meet at ReadData2_nq
  // Pins of 1 and 5 bits meet at Rt_nq
  // Pins of 1 and 5 bits meet at Rd_nq
  // Pins of 1 and 32 bits meet at Imm_nq
  // Pins of 1 and 32 bits meet at PC_plus_4_nq
  // Pins of 1 and 4 bits meet at ALUOp_nq
  // Pins of 1 and 32 bits meet at Jump_Address_nq
  // also tied to GND on the sheet: {RegWrite_nq, PC_plus_4_nq[0], ReadData1_nq[0], ReadData2_nq[0], Imm_nq[0], Rt_nq[0], Rd_nq[0], Jump_Address_nq[0], ALUSrc_nq, MemWrite_nq, ALUOp_nq[0], MemToReg_nq, MemRead_nq, Branch_nq, RegDst_nq, Jump_nq}
endmodule
