// Digital circuit IF_ID Reg.dig as structural Verilog
module IF_ID_Reg (
  input  CLK,
  input  [31:0] PC,
  input  [31:0] Instruction,
  input  [3:0] _28_31,
  output [31:0] PCOut,
  output [31:0] InstructionOut,
  output [3:0] _28_31Out
);

  wire [3:0] _28_31_nq;
  wire [31:0] Instruction_nq, PC_plus_4_nq;

  D_FF #(.Bits(32)) PC_plus_4 (.D(PC), .C(CLK), .Q(PCOut), .nQ(PC_plus_4_nq));
  D_FF #(.Bits(32)) u_Instruction (.D(Instruction), .C(CLK), .Q(InstructionOut), .nQ(Instruction_nq));
  D_FF #(.Bits(4)) u__28_31 (.D(_28_31), .C(CLK), .Q(_28_31Out), .nQ(_28_31_nq));
  // Pins of 1 and 32 bits meet at Instruction_nq
  // Pins of 1 and 32 bits meet at PC_plus_4_nq
  // Pins of 1 and 4 bits meet at _28_31_nq
  // also tied to GND on the sheet: {_28_31_nq[0], Instruction_nq[0], PC_plus_4_nq[0]}
endmodule
