// Digital circuit MEM_WB Reg.dig as structural Verilog
module MEM_WB_Reg (
  input  CLK,
  input  MemToReg,
  input  RegWrite,
  input  [31:0] ReadData,
  input  [31:0] RD2,
  input  [4:0] RegDst,
  output MemToRegOut,
  output RegWriteOut,
  output [31:0] ReadDataOut,
  output [31:0] RD2Out,
  output [4:0] RegDstOut
);

  wire MemToReg_nq, RegWrite_nq;
  wire [4:0] RegDst_nq;
  wire [31:0] RD2_nq, ReadData_nq;

  D_FF u_MemToReg (.D(MemToReg), .C(CLK), .Q(MemToRegOut), .nQ(MemToReg_nq));
  D_FF u_RegWrite (.D(RegWrite), .C(CLK), .Q(RegWriteOut), .nQ(RegWrite_nq));
  D_FF #(.Bits(32)) u_ReadData (.D(ReadData), .C(CLK), .Q(ReadDataOut), .nQ(ReadData_nq));
  D_FF #(.Bits(32)) u_RD2 (.D(RD2), .C(CLK), .Q(RD2Out), .nQ(RD2_nq));
  D_FF #(.Bits(5)) u_RegDst (.D(RegDst), .C(CLK), .Q(RegDstOut), .nQ(RegDst_nq));
  // Pins of 1 and 32 bits meet at ReadData_nq
  // Pins of 1 and 5 bits meet at RegDst_nq
  // Pins of 1 and 32 bits meet at RD2_nq
  // also tied to GND on the sheet: {MemToReg_nq, RegWrite_nq, ReadData_nq[0], RD2_nq[0], RegDst_nq[0]}
endmodule
