// Digital circuit Pipelined MIPS Datapath.dig as structural Verilog
module Pipelined_MIPS_Datapath (
);

  wire alu_1_zero, and_1_out, Branch_Add_c_o, CLK, controlunit_1_p3, controlunit_1_p4, controlunit_1_p5,
       controlunit_1_p6, controlunit_1_p7, controlunit_1_p8, controlunit_1_p9, controlunit_1_p10,
       controlunit_1_p11, ex_mem_reg_1_p14, ex_mem_reg_1_p15, ex_mem_reg_1_p16, ex_mem_reg_1_p17,
       ex_mem_reg_1_p18, ex_mem_reg_1_p19, ex_mem_reg_1_p21, ex_mem_reg_1_p24, ex_mem_reg_1_p25,
       id_ex_reg_1_p18, id_ex_reg_1_p19, id_ex_reg_1_p20, id_ex_reg_1_p21, id_ex_reg_1_p22, id_ex_reg_1_p24,
       id_ex_reg_1_p25, id_ex_reg_1_p26, id_ex_reg_1_p33, if_id_reg_1_p5, mem_wb_reg_1_p7, mem_wb_reg_1_p8,
       mem_wb_reg_1_p9, mem_wb_reg_1_p10, not_1_out, PC_plus_4_c_o;
  wire [3:0] id_ex_reg_1_p23, if_id_reg_1_p7, PC_plus_4_s_2;
  wire [4:0] id_ex_reg_1_p31, id_ex_reg_1_p32, mem_wb_reg_1_p11, multiplexer_4_out;
  wire [23:0] ex_mem_reg_1_p22;
  wire [27:0] PC_plus_4_s;
  wire [31:0] alu_1_result, barrelshifter_1_out, barrelshifter_2_out, bitextender_1_out, Branch_Add_s,
       Data_Memory_d, ex_mem_reg_1_p20, ex_mem_reg_1_p23, id_ex_reg_1_p27, id_ex_reg_1_p28, id_ex_reg_1_p29,
       id_ex_reg_1_p30, Instruction_Memory_d, multiplexer_1_out, multiplexer_2_out, multiplexer_3_out,
       multiplexer_5_out, PC_q, Register_File_da, Register_File_db;
  wire [31:26] undriven;
  wire [31:28] undriven_2;
  wire [32:0] if_id_reg_1_p6;

  Register #(.Bits(32), .isProgramCounter("true")) PC (.D(multiplexer_2_out), .C(CLK), .Q(PC_q));  // open: en
  Multiplexer #(.Bits(32)) multiplexer_1 (
    .sel(and_1_out), .in_0({PC_plus_4_s_2, PC_plus_4_s}), .in_1(ex_mem_reg_1_p20), .out(multiplexer_1_out));
  Add #(.Bits(32)) PC_plus_4 (
    .a(PC_q), .b({undriven_2, 28'h4}), .c_i(1'b0), .s({PC_plus_4_s_2, PC_plus_4_s}), .c_o(PC_plus_4_c_o));
  ROM #(.AddrBits(24), .isProgramMemory("true"), .Bits(32)) Instruction_Memory (
    .A(PC_q[23:0]), .sel(1'b1), .D(Instruction_Memory_d));
  Multiplexer multiplexer_2 (
    .sel(ex_mem_reg_1_p14), .in_0(multiplexer_1_out[0]), .in_1(ex_mem_reg_1_p25), .out(multiplexer_2_out[0]));
  // IF_ID_Reg if_id_reg_1: pin names not known; wires that end beside it: {PC_plus_4_s_2, PC_plus_4_s}, Instruction_Memory_d, PC_plus_4_s_2, CLK, if_id_reg_1_p5, if_id_reg_1_p6, if_id_reg_1_p7
  // ControlUnit controlunit_1: pin names not known; wires that end beside it: if_id_reg_1_p6[31:26], if_id_reg_1_p6[5:0], controlunit_1_p3, controlunit_1_p4, controlunit_1_p5, controlunit_1_p6, controlunit_1_p7, controlunit_1_p8, controlunit_1_p9, controlunit_1_p10, controlunit_1_p11
  not not_1 (not_1_out, CLK);
  BarrelShifter #(.Bits(32)) barrelshifter_1 (
    .in({undriven, if_id_reg_1_p6[25:0]}), .shift(26'h2), .out(barrelshifter_1_out));
  RegisterFile #(.AddrBits(5), .Bits(32)) Register_File (
    .Din(multiplexer_5_out), .we(mem_wb_reg_1_p8), .Rw(mem_wb_reg_1_p11), .C(not_1_out),
    .Ra(if_id_reg_1_p6[25:21]), .Rb(if_id_reg_1_p6[20:16]), .Da(Register_File_da), .Db(Register_File_db));
  BitExtender #(.inputBits(16), .outputBits(32)) bitextender_1 (.in(if_id_reg_1_p6[15:0]), .out(bitextender_1_out));
  // ID_EX_Reg id_ex_reg_1: pin names not known; wires that end beside it: controlunit_1_p3, controlunit_1_p4, controlunit_1_p5, controlunit_1_p6, controlunit_1_p7, controlunit_1_p8, controlunit_1_p9, controlunit_1_p10, controlunit_1_p11, if_id_reg_1_p5, Register_File_da, Register_File_db, bitextender_1_out, if_id_reg_1_p6[20:16], if_id_reg_1_p6[15:11], {if_id_reg_1_p7, barrelshifter_1_out[27:0]}, CLK, id_ex_reg_1_p18, id_ex_reg_1_p19, id_ex_reg_1_p20, id_ex_reg_1_p21, id_ex_reg_1_p22, id_ex_reg_1_p23, id_ex_reg_1_p24, id_ex_reg_1_p25, id_ex_reg_1_p26, id_ex_reg_1_p27, id_ex_reg_1_p28, id_ex_reg_1_p29, id_ex_reg_1_p30, id_ex_reg_1_p31, id_ex_reg_1_p32, id_ex_reg_1_p33
  BarrelShifter #(.Bits(32)) barrelshifter_2 (.in(id_ex_reg_1_p30), .shift(2'b10), .out(barrelshifter_2_out));
  Multiplexer #(.Bits(32)) multiplexer_3 (
    .sel(id_ex_reg_1_p25), .in_0(id_ex_reg_1_p29), .in_1(id_ex_reg_1_p30), .out(multiplexer_3_out));
  Add #(.Bits(32)) Branch_Add (
    .a(id_ex_reg_1_p27), .b(barrelshifter_2_out), .c_i(1'b0), .s(Branch_Add_s), .c_o(Branch_Add_c_o));
  Multiplexer #(.Bits(5)) multiplexer_4 (
    .sel(id_ex_reg_1_p19), .in_0(id_ex_reg_1_p31), .in_1(id_ex_reg_1_p32), .out(multiplexer_4_out));
  ALU alu_1 (
    .Op1(id_ex_reg_1_p28), .Op2(multiplexer_3_out), .Opcode(id_ex_reg_1_p23), .Zero(alu_1_zero),
    .Result(alu_1_result));
  // EX_MEM_Reg ex_mem_reg_1: pin names not known; wires that end beside it: id_ex_reg_1_p18, id_ex_reg_1_p20, id_ex_reg_1_p21, id_ex_reg_1_p22, id_ex_reg_1_p24, id_ex_reg_1_p26, Branch_Add_s, alu_1_zero, alu_1_result, id_ex_reg_1_p29, multiplexer_4_out, id_ex_reg_1_p33, CLK, ex_mem_reg_1_p14, ex_mem_reg_1_p15, ex_mem_reg_1_p16, ex_mem_reg_1_p17, ex_mem_reg_1_p18, ex_mem_reg_1_p19, ex_mem_reg_1_p20, ex_mem_reg_1_p21, ex_mem_reg_1_p22, ex_mem_reg_1_p23, ex_mem_reg_1_p24, ex_mem_reg_1_p25
  and and_1 (and_1_out, ex_mem_reg_1_p15, ex_mem_reg_1_p21);
  RAMDualPort #(.AddrBits(24), .Bits(32)) Data_Memory (
    .A(ex_mem_reg_1_p22), .Din(ex_mem_reg_1_p23), .str(ex_mem_reg_1_p18), .C(CLK), .ld(ex_mem_reg_1_p16),
    .D(Data_Memory_d));
  // MEM_WB_Reg mem_wb_reg_1: pin names not known; wires that end beside it: ex_mem_reg_1_p17, ex_mem_reg_1_p19, Data_Memory_d, ex_mem_reg_1_p23, ex_mem_reg_1_p24, CLK, mem_wb_reg_1_p7, mem_wb_reg_1_p8, mem_wb_reg_1_p9, mem_wb_reg_1_p10, mem_wb_reg_1_p11
  Multiplexer multiplexer_5 (
    .sel(mem_wb_reg_1_p7), .in_0(mem_wb_reg_1_p10), .in_1(mem_wb_reg_1_p9), .out(multiplexer_5_out[0]));
  // Pins of 1 and 32 bits meet at multiplexer_2_out
  // Pins of 24 and 32 bits meet at PC_q
  // Pins of 28 and 32 bits meet at {undriven_2, 28'h4}
  // Pins of 1 and 32 bits meet at multiplexer_5_out
  // Pins of 1 and 32 bits meet at multiplexer_1_out
  // Pins of 26 and 32 bits meet at {undriven, if_id_reg_1_p6[25:0]}
  // Pins of 28 and 32 bits meet at barrelshifter_1_out
  // also tied to GND on the sheet: {Branch_Add_c_o, PC_plus_4_c_o}
endmodule
